# Fritzing sketch 5641AS_Arduino_Connection (saved by Fritzing 0.9.10b)
breadboards: 1

parts:
  7_Segment_4_Digit_Display1 = 7-SEGMENT-4DIGIT common anode [part_number="5461BS - 5462BS" package=7-segment-4digit-anode]
  Part1 = Arduino Uno (Rev3)
  R1 = Resistor [tolerance=±5% resistance=220 package="0402 [SMD]"]
  R2 = Resistor [tolerance=±5% resistance=220 package="0402 [SMD]"]
  R3 = Resistor [tolerance=±5% resistance=220 package="0402 [SMD]"]
  R4 = Resistor [tolerance=±5% resistance=220 package="0402 [SMD]"]

nets:
  N1: 7_Segment_4_Digit_Display1.pin_1, Part1.D10_PWM/SS
  N2: 7_Segment_4_Digit_Display1.pin_2, Part1.D9_PWM
  N3: 7_Segment_4_Digit_Display1.pin_3, Part1.D13/SCK
  N4: 7_Segment_4_Digit_Display1.pin_4, Part1.D8
  N5: 7_Segment_4_Digit_Display1.pin_5, Part1.D12/MISO
  N6: 7_Segment_4_Digit_Display1.pin_6, R1.Pin_0
  N7: 7_Segment_4_Digit_Display1.pin_7, Part1.D7
  N8: 7_Segment_4_Digit_Display1.pin_8, R2.Pin_0
  N9: 7_Segment_4_Digit_Display1.pin_9, R3.Pin_0
  N10: 7_Segment_4_Digit_Display1.pin_10, Part1.D11_PWM/MOSI
  N11: 7_Segment_4_Digit_Display1.pin_11, Part1.D6_PWM
  N12: 7_Segment_4_Digit_Display1.pin_12, R4.Pin_0
  N13: Part1.D2, R4.Pin_1
  N14: Part1.D3_PWM, R3.Pin_1
  N15: Part1.D4, R2.Pin_1
  N16: Part1.D5_PWM, R1.Pin_1

notes:
  Need atleast 4 220ohm Resistors

custom parts:
  7-SEGMENT-4DIGIT common anode: A 7 Segment 4 Digit common anode display, with decimal points
