# Fritzing sketch 2PinActiveBuzzer (saved by Fritzing 0.9.10b)
breadboards: 1

parts:
  Part1 = Arduino Mega ADK (Rev3)
  active_buzzer1 = Active buzzer [package=THT]

nets:
  GND: Part1.GND, active_buzzer1.GND
  N1: Part1.D2_PWM, active_buzzer1.Vcc

custom parts:
  Active buzzer: Active buzzer 12 mm, 3-5 V
