# Fritzing sketch OnePotentiometer (saved by Fritzing 0.9.10b)
breadboards: 1

parts:
  Part1 = Arduino Mega ADK (Rev3)
  R1 = Trimmer Potentiometer [maximum_resistance=10kΩ knob_status=50% power=0.5W package=THT]

nets:
  N1: Part1.A0, R1.wiper
  N2: Part1.GND, R1.leg1
  N3: Part1.5V, R1.leg2
