# Fritzing sketch UltrasonicSensor-HC-SR04 (saved by Fritzing 0.9.10b)
breadboards: 1

parts:
  Part1 = Arduino Mega 2560 (Rev3)
  HC-SR04_Sensor_1 = HC-SR04 Ultrasonic Distance Sensor

nets:
  N1: Part1.D13_PWM, HC-SR04_Sensor_1.TRIG
  N2: Part1.D12_PWM, HC-SR04_Sensor_1.ECHO
  5V: Part1.5V, HC-SR04_Sensor_1.VCC
