# Fritzing sketch 1Digit7SegmentLED (saved by Fritzing 0.9.10b)
breadboards: 1

parts:
  Part1 = Arduino Mega 2560 (Rev3)
  7_Segment4 = 7 Segment Display
  R1 = Resistor [tolerance=±5% power=0.25 resistance=220 package=THT]
  R2 = Resistor [tolerance=±5% power=0.25 resistance=220 package=THT]

nets:
  N1: Part1.GND, R1.Pin_0, R2.Pin_1
  N2: Part1.D8_PWM, 7_Segment4.Segment_G
  N3: Part1.D2_PWM, 7_Segment4.Segment_A
  N4: Part1.D3_PWM, 7_Segment4.Segment_B
  N5: Part1.D4_PWM, 7_Segment4.Segment_C
  N6: Part1.D5_PWM, 7_Segment4.Segment_D
  N7: Part1.D6_PWM, 7_Segment4.Segment_E
  N8: Part1.D7_PWM, 7_Segment4.Segment_F
  N9: 7_Segment4.common_cathode, R1.Pin_1, R2.Pin_0
