# Fritzing sketch PIRMotionSensor (saved by Fritzing 0.9.10b)
breadboards: 1

parts:
  PIR1 = PIR sensor
  LED2 = LED - 5mm [color="Red (633nm)" current=0.030 package="5 mm [THT]"]
  J1 = Piezo Speaker
  R1 = Resistor [tolerance=±5% resistance=220 package="0805 [SMD]"]
  Part1 = Arduino Mega 2560 (Rev3)

nets:
  N1: PIR1.VDD, J1.pin2
  N2: PIR1.SIG, Part1.D2_PWM
  GND: PIR1.GND, LED2.cathode, J1.pin1, Part1.GND
  N3: LED2.anode, R1.Pin_1
  N4: R1.Pin_0, Part1.D3_PWM
