# Fritzing sketch 2-Pin Passive Buzzer (saved by Fritzing 0.9.10b)
breadboards: 1

parts:
  Part1 = Arduino Mega ADK (Rev3)
  passive_buzzer1 = Passive buzzer [package=THT]

nets:
  N1: Part1.GND, passive_buzzer1.pin2
  N2: Part1.D2_PWM, passive_buzzer1.pin1

custom parts:
  Passive buzzer: Passive buzzer 12 mm, 3-5 V
