# Fritzing sketch LCD1602_LCD_Display (saved by Fritzing 0.9.10b)
breadboards: 1

parts:
  Part1 = Arduino Mega 2560 (Rev3)
  LCD1 = LCD screen
  R4 = Trimmer Potentiometer [maximum_resistance=10kΩ knob_status=50% power=0.5W package=THT]
  R5 = Resistor [tolerance=±5% power=0.25 resistance=220 package=THT]

nets:
  GND: Part1.GND, LCD1.VSS, LCD1.R/W, LCD1.LED-, R4.leg2
  N1: Part1.D12_PWM, LCD1.RS
  N2: Part1.D11_PWM, LCD1.E
  5V: Part1.5V, LCD1.VDD, R4.leg1, R5.Pin_0
  N3: Part1.D2_PWM, LCD1.DB4
  N4: Part1.D3_PWM, LCD1.DB5
  N5: Part1.D4_PWM, LCD1.DB6
  N6: Part1.D5_PWM, LCD1.DB7
  N7: LCD1.V0, R4.wiper
  N8: LCD1.LED+, R5.Pin_1
