# Fritzing sketch RGB-LightEmittingDiode (saved by Fritzing 0.9.10b)
breadboards: 1

parts:
  LED2 = RGB LED (com. anode, rbg) [package="5 mm [THT]"]
  R1 = Resistor [tolerance=±5% power=0.25 resistance=220 package=THT]
  R2 = Resistor [tolerance=±5% power=0.25 resistance=220 package=THT]
  R3 = Resistor [tolerance=±5% power=0.25 resistance=220 package=THT]
  Part1 = Arduino Mega 2560 (Rev3)

nets:
  N1: LED2.red_cathode, R1.Pin_0
  N2: LED2.common_anode, Part1.GND
  N3: LED2.blue_cathode, R3.Pin_0
  N4: LED2.green_cathode, R2.Pin_0
  N5: R1.Pin_1, Part1.D7_PWM
  N6: R2.Pin_1, Part1.D5_PWM
  N7: R3.Pin_1, Part1.D6_PWM

custom parts:
  Arduino Mega 2560 (Rev3): The Arduino Mega 2560 is a microcontroller board based on the ATmega2560 (datasheet). It has 54 digital input/output pins (of which 14 can be used as PWM outputs), 16 analog inputs, 4 UARTs (hardware serial ports), a 16 MHz crystal oscillator, a USB connection, a power jack, an ICSP header, and a reset button. It contains everything needed to support the microcontroller; simply connect it to a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
