# Fritzing sketch 2PinActiveBuzzer (saved by Fritzing 0.9.10b)
breadboards: 1

parts:
  active_buzzer1 = Active buzzer [package=THT]
  Part2 = Arduino Mega 2560 (Rev3)

nets:
  GND: active_buzzer1.GND, Part2.GND
  N1: active_buzzer1.Vcc, Part2.D2_PWM

custom parts:
  Active buzzer: Active buzzer 12 mm, 3-5 V
  Arduino Mega 2560 (Rev3): The Arduino Mega 2560 is a microcontroller board based on the ATmega2560 (datasheet). It has 54 digital input/output pins (of which 14 can be used as PWM outputs), 16 analog inputs, 4 UARTs (hardware serial ports), a 16 MHz crystal oscillator, a USB connection, a power jack, an ICSP header, and a reset button. It contains everything needed to support the microcontroller; simply connect it to a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
