# Fritzing sketch 3PinActiveBuzzer (saved by Fritzing 0.9.10b)
breadboards: 1

parts:
  Mod2 = KY-012 Active Buzzer Module [package="Breakout board"]
  Part2 = Arduino Mega 2560 (Rev3)

nets:
  N1: Mod2.S, Part2.D2_PWM
  N2: Mod2.-, Part2.GND

custom parts:
  KY-012 Active Buzzer Module: Active Piezoelectric Buzzer Module KY-012, it produces single-tone sound when signal is high. (Special thanks to vanepp for fixing the PCB holes and other errors)
  Arduino Mega 2560 (Rev3): The Arduino Mega 2560 is a microcontroller board based on the ATmega2560 (datasheet). It has 54 digital input/output pins (of which 14 can be used as PWM outputs), 16 analog inputs, 4 UARTs (hardware serial ports), a 16 MHz crystal oscillator, a USB connection, a power jack, an ICSP header, and a reset button. It contains everything needed to support the microcontroller; simply connect it to a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
