# Fritzing sketch OnePotentiometer (saved by Fritzing 0.9.10b)
breadboards: 1

parts:
  R1 = Trimmer Potentiometer [maximum_resistance=10kΩ knob_status=50% power=0.5W package=THT]
  Part2 = Arduino Mega 2560 (Rev3)

nets:
  N1: R1.leg1, Part2.GND
  N2: R1.wiper, Part2.A0
  N3: R1.leg2, Part2.5V

custom parts:
  Arduino Mega 2560 (Rev3): The Arduino Mega 2560 is a microcontroller board based on the ATmega2560 (datasheet). It has 54 digital input/output pins (of which 14 can be used as PWM outputs), 16 analog inputs, 4 UARTs (hardware serial ports), a 16 MHz crystal oscillator, a USB connection, a power jack, an ICSP header, and a reset button. It contains everything needed to support the microcontroller; simply connect it to a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
