# Fritzing sketch IrReceiver (saved by Fritzing 0.9.10b)
breadboards: 1

parts:
  Part1 = Arduino Mega 2560 (Rev3)
  Mod1 = KY-022 Infrared Receiver Module [package="Breakout board"]

nets:
  N1: Part1.D11_PWM, Mod1.S
  5V: Part1.5V, Mod1.Vin
  N2: Part1.GND, Mod1.-

custom parts:
  KY-022 Infrared Receiver Module: KY-022 IR receiver module, reacts to 38kHz infrared light.
