# Fritzing sketch UltrasonicSensor-HC-SR04 (saved by Fritzing 0.9.10b)
breadboards: 1

parts:
  HC-SR04_Sensor_1 = HC-SR04 Ultrasonic Distance Sensor
  Part2 = Arduino Mega 2560 (Rev3)

nets:
  VCC: HC-SR04_Sensor_1.VCC, Part2.5V
  N1: HC-SR04_Sensor_1.TRIG, Part2.D13_PWM
  N2: HC-SR04_Sensor_1.ECHO, Part2.D12_PWM

custom parts:
  Arduino Mega 2560 (Rev3): The Arduino Mega 2560 is a microcontroller board based on the ATmega2560 (datasheet). It has 54 digital input/output pins (of which 14 can be used as PWM outputs), 16 analog inputs, 4 UARTs (hardware serial ports), a 16 MHz crystal oscillator, a USB connection, a power jack, an ICSP header, and a reset button. It contains everything needed to support the microcontroller; simply connect it to a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
