# Fritzing sketch 4x4_MembraneKeypad (saved by Fritzing 0.9.10b)
breadboards: 1

parts:
  Keypad4x1 = Keypad Membran 4x4
  Part2 = Arduino Mega 2560 (Rev3)

nets:
  N1: Keypad4x1.Pin1, Part2.D9_PWM
  N2: Keypad4x1.Pin2, Part2.D8_PWM
  N3: Keypad4x1.Pin3, Part2.D7_PWM
  N4: Keypad4x1.Pin4, Part2.D6_PWM
  N5: Keypad4x1.Pin5, Part2.D5_PWM
  N6: Keypad4x1.Pin6, Part2.D4_PWM
  N7: Keypad4x1.Pin7, Part2.D3_PWM
  N8: Keypad4x1.Pin8, Part2.D2_PWM

custom parts:
  Keypad Membran 4x4: Membrane Keypad 4x4 Matrix
  Arduino Mega 2560 (Rev3): The Arduino Mega 2560 is a microcontroller board based on the ATmega2560 (datasheet). It has 54 digital input/output pins (of which 14 can be used as PWM outputs), 16 analog inputs, 4 UARTs (hardware serial ports), a 16 MHz crystal oscillator, a USB connection, a power jack, an ICSP header, and a reset button. It contains everything needed to support the microcontroller; simply connect it to a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
