# Fritzing sketch RFID-Reader (saved by Fritzing 0.9.10b)
breadboards: 1

parts:
  Part1 = RFID-RC522-v3
  Part2 = Arduino Mega 2560 (Rev3)

nets:
  N1: Part1.SDA, Part2.3V3
  N2: Part1.SCK, Part2.D8_PWM
  N3: Part1.IRQ, Part2.D50
  N4: Part1.GND, Part2.D51
  N5: Part1.RST, Part2.D52
  N6: Part1.3.3V, Part2.D53

notes:
  3.3v power ONLY

custom parts:
  RFID-RC522-v3: A simple China made RFID-RC522 Reader (6x4 cm); do check the pin labels, as this is a MFRC522 based clone.
  Arduino Mega 2560 (Rev3): The Arduino Mega 2560 is a microcontroller board based on the ATmega2560 (datasheet). It has 54 digital input/output pins (of which 14 can be used as PWM outputs), 16 analog inputs, 4 UARTs (hardware serial ports), a 16 MHz crystal oscillator, a USB connection, a power jack, an ICSP header, and a reset button. It contains everything needed to support the microcontroller; simply connect it to a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
