# Fritzing sketch LightEmittingDiode (saved by Fritzing 0.9.10b)
breadboards: 1

parts:
  LED2 = smd LED [color="Red (633nm)" package="1206 [SMD]"]
  R1 = Resistor [tolerance=±5% resistance=220 package="0603 [SMD]"]
  Mod1 = ESP32-TTGO-T-DISPLAY

nets:
  N1: LED2.cathode, R1.Pin_0
  N2: LED2.anode, Mod1.32
  N3: R1.Pin_1, Mod1.G-1

notes:
  220 Ohm resistor

custom parts:
  ESP32-TTGO-T-DISPLAY: LILYGO TTGO T-Display GD32VF103CBT6 Main Chip ST7789 1.14 Inch IPS 240x135 Resolution Minimalist Development Board.
