# Fritzing sketch RGB-LightEmittingDiode (saved by Fritzing 0.9.10b)
breadboards: 1

parts:
  LED2 = RGB LED (com. anode, rbg) [package="5 mm [THT]"]
  R1 = Resistor [tolerance=±5% power=0.25 resistance=220 package=THT]
  R2 = Resistor [tolerance=±5% power=0.25 resistance=220 package=THT]
  R3 = Resistor [tolerance=±5% power=0.25 resistance=220 package=THT]
  Mod1 = ESP32-TTGO-T-DISPLAY

nets:
  N1: LED2.red_cathode, R1.Pin_0
  N2: LED2.common_anode, Mod1.G-1, Mod1.G-14
  N3: LED2.blue_cathode, R3.Pin_0
  N4: LED2.green_cathode, R2.Pin_0
  N5: R1.Pin_1, Mod1.13
  N6: R2.Pin_1, Mod1.2
  N7: R3.Pin_1, Mod1.15

custom parts:
  ESP32-TTGO-T-DISPLAY: LILYGO TTGO T-Display GD32VF103CBT6 Main Chip ST7789 1.14 Inch IPS 240x135 Resolution Minimalist Development Board.
