# Fritzing sketch PhotoResistor (saved by Fritzing 0.9.10b)
breadboards: 1

parts:
  Part1 = Arduino Mega 2560 (Rev3)
  R1 = PHOTOCELL [package=photocell]
  R2 = Resistor [tolerance=±5% power=0.25 resistance=10k package=THT]

nets:
  N1: Part1.A0, R1.P$1, R2.Pin_1
  N2: Part1.GND, R2.Pin_0
  N3: Part1.5V, R1.P$2

notes:
  10k Ohm resistor

custom parts:
  Arduino Mega 2560 (Rev3): The Arduino Mega 2560 is a microcontroller board based on the ATmega2560 (datasheet). It has 54 digital input/output pins (of which 14 can be used as PWM outputs), 16 analog inputs, 4 UARTs (hardware serial ports), a 16 MHz crystal oscillator, a USB connection, a power jack, an ICSP header, and a reset button. It contains everything needed to support the microcontroller; simply connect it to a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
