# Fritzing sketch 3PinPassiveBuzzer (saved by Fritzing 0.9.10b)
breadboards: 1

parts:
  Part1 = Arduino Mega ADK (Rev3)
  Part2 = KY-006 Passive Buzzer Module [package="Breakout board"]

nets:
  N1: Part1.GND, Part2.-
  N2: Part1.D2_PWM, Part2.S

custom parts:
  KY-006 Passive Buzzer Module: Passive Piezoelectric Buzzer Module Keyes KY-006, it can produce a range of sound tones depending on the input frequency.
