# Fritzing sketch RotaryEncoder (saved by Fritzing 0.9.10b)
breadboards: 1

parts:
  Part1 = Arduino Mega 2560 (Rev3)
  RE1 = KY-040 Rotary encoder [package=THT]

nets:
  GND: Part1.GND, RE1.GND
  5V: Part1.5V, RE1.Vcc
  N1: Part1.D2_PWM, RE1.CLK
  N2: Part1.D3_PWM, RE1.DT
  N3: Part1.D4_PWM, RE1.SW

custom parts:
  Arduino Mega 2560 (Rev3): The Arduino Mega 2560 is a microcontroller board based on the ATmega2560 (datasheet). It has 54 digital input/output pins (of which 14 can be used as PWM outputs), 16 analog inputs, 4 UARTs (hardware serial ports), a 16 MHz crystal oscillator, a USB connection, a power jack, an ICSP header, and a reset button. It contains everything needed to support the microcontroller; simply connect it to a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
  KY-040 Rotary encoder: KY-040 Rotary Encoder with switch on breakout borad from AZ Delivery
