# Fritzing sketch IrReceiver (saved by Fritzing 0.9.10b)
breadboards: 1

parts:
  Mod1 = KY-022 Infrared Receiver Module [package="Breakout board"]
  Part2 = Arduino Mega 2560 (Rev3)

nets:
  N1: Mod1.-, Part2.GND
  VIN: Mod1.Vin, Part2.5V
  N2: Mod1.S, Part2.D11_PWM

custom parts:
  KY-022 Infrared Receiver Module: KY-022 IR receiver module, reacts to 38kHz infrared light.
  Arduino Mega 2560 (Rev3): The Arduino Mega 2560 is a microcontroller board based on the ATmega2560 (datasheet). It has 54 digital input/output pins (of which 14 can be used as PWM outputs), 16 analog inputs, 4 UARTs (hardware serial ports), a 16 MHz crystal oscillator, a USB connection, a power jack, an ICSP header, and a reset button. It contains everything needed to support the microcontroller; simply connect it to a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
