# Fritzing sketch 1Digit7SegmentLED (saved by Fritzing 0.9.10b)
breadboards: 1

parts:
  7_Segment4 = 7 Segment Display
  R1 = Resistor [tolerance=±5% power=0.25 resistance=220 package=THT]
  R2 = Resistor [tolerance=±5% power=0.25 resistance=220 package=THT]
  Part2 = Arduino Mega 2560 (Rev3)

nets:
  N1: 7_Segment4.Segment_E, Part2.D6_PWM
  N2: 7_Segment4.Segment_D, Part2.D5_PWM
  N3: 7_Segment4.common_cathode, R1.Pin_1, R2.Pin_0
  N4: 7_Segment4.Segment_C, Part2.D4_PWM
  N5: 7_Segment4.Segment_B, Part2.D3_PWM
  N6: 7_Segment4.Segment_A, Part2.D2_PWM
  N7: 7_Segment4.Segment_F, Part2.D7_PWM
  N8: 7_Segment4.Segment_G, Part2.D8_PWM
  N9: R1.Pin_0, R2.Pin_1, Part2.GND

custom parts:
  Arduino Mega 2560 (Rev3): The Arduino Mega 2560 is a microcontroller board based on the ATmega2560 (datasheet). It has 54 digital input/output pins (of which 14 can be used as PWM outputs), 16 analog inputs, 4 UARTs (hardware serial ports), a 16 MHz crystal oscillator, a USB connection, a power jack, an ICSP header, and a reset button. It contains everything needed to support the microcontroller; simply connect it to a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
