# Fritzing sketch GameJoystick (saved by Fritzing 0.9.10b)

parts:
  Part1 = Arduino Mega 2560 (Rev3)
  Mod1 = KY-023 Dual Axis Joystick Module [package="Breakout board"]

nets:
  N1: Part1.A0, Mod1.VRx
  N2: Part1.A1, Mod1.VRy
  5V: Part1.5V, Mod1.+5V
  GND: Part1.GND, Mod1.GND
  N3: Part1.D2_PWM, Mod1.SW

custom parts:
  Arduino Mega 2560 (Rev3): The Arduino Mega 2560 is a microcontroller board based on the ATmega2560 (datasheet). It has 54 digital input/output pins (of which 14 can be used as PWM outputs), 16 analog inputs, 4 UARTs (hardware serial ports), a 16 MHz crystal oscillator, a USB connection, a power jack, an ICSP header, and a reset button. It contains everything needed to support the microcontroller; simply connect it to a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
  KY-023 Dual Axis Joystick Module: KY-023 Dual-Axis Joystick Module.
