# Fritzing sketch SoundSensor - KY-038 (saved by Fritzing 0.9.10b)
breadboards: 1

parts:
  Part1 = Arduino Mega 2560 (Rev3)
  Mic1 = KY-038

nets:
  N1: Part1.A0, Mic1.pin1
  N2: Part1.5V, Mic1.pin3
  N3: Part1.GND, Mic1.pin2
  N4: Part1.D2_PWM, Mic1.pin4

custom parts:
  Arduino Mega 2560 (Rev3): The Arduino Mega 2560 is a microcontroller board based on the ATmega2560 (datasheet). It has 54 digital input/output pins (of which 14 can be used as PWM outputs), 16 analog inputs, 4 UARTs (hardware serial ports), a 16 MHz crystal oscillator, a USB connection, a power jack, an ICSP header, and a reset button. It contains everything needed to support the microcontroller; simply connect it to a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
  KY-038: ky-038 Microphone sound sensor module
