# Fritzing sketch ServoMotor (saved by Fritzing 0.9.10b)

parts:
  Part2 = Arduino Mega 2560 (Rev3)
  J1 = Basic Servo

nets:
  GND: Part2.GND, J1.gnd
  N1: Part2.D9_PWM, J1.pulse
  5V: Part2.5V, J1.vcc

custom parts:
  Arduino Mega 2560 (Rev3): The Arduino Mega 2560 is a microcontroller board based on the ATmega2560 (datasheet). It has 54 digital input/output pins (of which 14 can be used as PWM outputs), 16 analog inputs, 4 UARTs (hardware serial ports), a 16 MHz crystal oscillator, a USB connection, a power jack, an ICSP header, and a reset button. It contains everything needed to support the microcontroller; simply connect it to a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
