# Fritzing sketch LCD1602_LCD_Display (saved by Fritzing 0.9.10b)
breadboards: 1

parts:
  LCD1 = LCD screen
  R4 = Trimmer Potentiometer [maximum_resistance=10kΩ knob_status=50% power=0.5W package=THT]
  R5 = Resistor [tolerance=±5% power=0.25 resistance=220 package=THT]
  Part2 = Arduino Mega 2560 (Rev3)

nets:
  VSS: LCD1.VSS, LCD1.R/W, LCD1.LED-, R4.leg2, Part2.GND
  VDD: LCD1.VDD, R4.leg1, R5.Pin_0, Part2.5V
  N1: LCD1.V0, R4.wiper
  N2: LCD1.RS, Part2.D12_PWM
  N3: LCD1.E, Part2.D11_PWM
  N4: LCD1.DB4, Part2.D2_PWM
  N5: LCD1.DB5, Part2.D3_PWM
  N6: LCD1.DB6, Part2.D4_PWM
  N7: LCD1.DB7, Part2.D5_PWM
  N8: LCD1.LED+, R5.Pin_1

custom parts:
  Arduino Mega 2560 (Rev3): The Arduino Mega 2560 is a microcontroller board based on the ATmega2560 (datasheet). It has 54 digital input/output pins (of which 14 can be used as PWM outputs), 16 analog inputs, 4 UARTs (hardware serial ports), a 16 MHz crystal oscillator, a USB connection, a power jack, an ICSP header, and a reset button. It contains everything needed to support the microcontroller; simply connect it to a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
