# Fritzing sketch L293D_MotorDriverIC (saved by Fritzing 0.9.10b)
breadboards: 1

parts:
  Part1 = Arduino Mega 2560 (Rev3)
  IC1 = L293D [package=THT]
  M1 = DC Motor [voltage_(max)=6V voltage_(min)=3V]
  YwRobot_Power_Supply1 = YwRobot Breadboard Power Supply [part_number=545043]

nets:
  N1: Part1.GND, IC1.0V, IC1.+Vmotor, YwRobot_Power_Supply1.GND#11
  N2: Part1.D5_PWM, IC1.In_1
  N3: Part1.D6_PWM, IC1.In_2
  N4: IC1.Enable_1, YwRobot_Power_Supply1.VCC#5
  N5: IC1.Out_1_(_Controlled_by_Enable_1_), M1.pin_2
  N6: IC1.Out_2_(_Controlled_by_Enable_1_), M1.pin_1

custom parts:
  Arduino Mega 2560 (Rev3): The Arduino Mega 2560 is a microcontroller board based on the ATmega2560 (datasheet). It has 54 digital input/output pins (of which 14 can be used as PWM outputs), 16 analog inputs, 4 UARTs (hardware serial ports), a 16 MHz crystal oscillator, a USB connection, a power jack, an ICSP header, and a reset button. It contains everything needed to support the microcontroller; simply connect it to a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
  YwRobot Breadboard Power Supply: The YwRobot Breadboard Power Supply (MB-V2) has two power rails; they can be 5V or 3V3. Power to the module can be provided through the female USB socket or through the A10 (female) 2.1mm power jack.
