# Fritzing sketch 20_ButtonInputPullDown (saved by Fritzing 0.9.10b)
breadboards: 1

parts:
  Part1 = Arduino Mega 2560 (Rev3)
  LED1 = LED - 5mm [color="Red (633nm)" current=0.030 package="5 mm [THT]"]
  R1 = Resistor [tolerance=±5% resistance=220 package="2010 [SMD]"]
  S1 = Pushbutton [package="[THT]"]
  R2 = Resistor [tolerance=±5% resistance=10 package="2512 [SMD]"]

nets:
  N1: Part1.5V, S1.Pin_3, S1.Pin_4
  N2: Part1.D22, LED1.anode
  N3: Part1.D23, S1.Pin_1, S1.Pin_2, R2.Pin_0
  N4: Part1.GND, R1.Pin_0, R2.Pin_1
  N5: LED1.cathode, R1.Pin_1

notes:
  NOTE: Resistors are connected to ground via the ground rail (blue line) on the breadboard.
  LED resistor: 220 Ohm
  Button pull-down: 10K Ohm

custom parts:
  Arduino Mega 2560 (Rev3): The Arduino Mega 2560 is a microcontroller board based on the ATmega2560 (datasheet). It has 54 digital input/output pins (of which 14 can be used as PWM outputs), 16 analog inputs, 4 UARTs (hardware serial ports), a 16 MHz crystal oscillator, a USB connection, a power jack, an ICSP header, and a reset button. It contains everything needed to support the microcontroller; simply connect it to a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
