# Fritzing sketch 20_DimmingTheLights (saved by Fritzing 0.9.10b)
breadboards: 1

parts:
  Part1 = Arduino Mega 2560 (Rev3)
  LED1 = LED - 5mm [color="Red (633nm)" current=0.030 package="5 mm [THT]"]
  R1 = Resistor [tolerance=±5% resistance=220 package="2010 [SMD]"]
  S1 = Pushbutton [package="[THT]"]
  R2 = Resistor [tolerance=±5% resistance=10k package="2010 [SMD]"]
  R3 = PHOTOCELL [package=photocell]
  SG1 = Buzzer 12mm [part_number=COM-07950 package=buzzer-12mm-ns]
  R6 = Trimmer Potentiometer [maximum_resistance=10kΩ knob_status=50% power=0.5W package=THT]

nets:
  N1: Part1.A8, R2.Pin_1, R3.P$1
  N2: Part1.A9, R6.wiper
  N3: Part1.5V, R3.P$2, R6.leg1
  N4: Part1.D23, S1.Pin_1, S1.Pin_2
  N5: Part1.D24, SG1.1
  N6: Part1.D44, LED1.anode
  N7: Part1.GND, R1.Pin_0, S1.Pin_3, S1.Pin_4, R2.Pin_0, R6.leg2
  N8: LED1.cathode, R1.Pin_1

notes:
  We now need a pin that can do PWM so LED is now on pin 44

custom parts:
  Arduino Mega 2560 (Rev3): The Arduino Mega 2560 is a microcontroller board based on the ATmega2560 (datasheet). It has 54 digital input/output pins (of which 14 can be used as PWM outputs), 16 analog inputs, 4 UARTs (hardware serial ports), a 16 MHz crystal oscillator, a USB connection, a power jack, an ICSP header, and a reset button. It contains everything needed to support the microcontroller; simply connect it to a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
  Buzzer 12mm: Buzzer 12mm Spark Fun Electronics SKU : Comp-Buzzer Through hole This is a small 12mm round speaker that operates around the audible 2kHz range. You can use these speakers to create simple music or user interfaces. This is not a true piezoelectric speaker but behaves similarly. Instead of a piezoelectric crystal that vibrates with an electric current, this tiny speaker uses an electromagnet to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
