# Fritzing sketch 01_MotionSensorLights (saved by Fritzing 0.9.10b)
breadboards: 1

parts:
  Part1 = Arduino Mega 2560 (Rev3)
  LED1 = LED - 5mm [color="Red (633nm)" current=0.030 package="5 mm [THT]"]
  R1 = Resistor [tolerance=±5% power=0.25 resistance=220 package=THT]
  PIR2 = PIR sensor

nets:
  5V: Part1.5V, PIR2.VDD
  N1: Part1.D22, R1.Pin_1
  N2: Part1.D23, PIR2.SIG
  GND: Part1.GND, LED1.cathode, PIR2.GND
  N3: LED1.anode, R1.Pin_0

custom parts:
  Arduino Mega 2560 (Rev3): The Arduino Mega 2560 is a microcontroller board based on the ATmega2560 (datasheet). It has 54 digital input/output pins (of which 14 can be used as PWM outputs), 16 analog inputs, 4 UARTs (hardware serial ports), a 16 MHz crystal oscillator, a USB connection, a power jack, an ICSP header, and a reset button. It contains everything needed to support the microcontroller; simply connect it to a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
