# Fritzing sketch 02_KeypadDoorLock (saved by Fritzing 0.9.10b)
breadboards: 1

parts:
  Part1 = Arduino Mega 2560 (Rev3)
  Keypad4x1 = Keypad Membran 4x4

nets:
  N1: Part1.D23, Keypad4x1.Pin1
  N2: Part1.D25, Keypad4x1.Pin2
  N3: Part1.D27, Keypad4x1.Pin3
  N4: Part1.D29, Keypad4x1.Pin4
  N5: Part1.D31, Keypad4x1.Pin5
  N6: Part1.D33, Keypad4x1.Pin6
  N7: Part1.D35, Keypad4x1.Pin7
  N8: Part1.D37, Keypad4x1.Pin8

custom parts:
  Arduino Mega 2560 (Rev3): The Arduino Mega 2560 is a microcontroller board based on the ATmega2560 (datasheet). It has 54 digital input/output pins (of which 14 can be used as PWM outputs), 16 analog inputs, 4 UARTs (hardware serial ports), a 16 MHz crystal oscillator, a USB connection, a power jack, an ICSP header, and a reset button. It contains everything needed to support the microcontroller; simply connect it to a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
  Keypad Membran 4x4: Membrane Keypad 4x4 Matrix
