# Fritzing sketch 40_KeypadDoorLock (saved by Fritzing 0.9.10b)
breadboards: 1

parts:
  Part1 = Arduino Mega 2560 (Rev3)
  Keypad4x1 = Keypad Membran 4x4
  U1 = LCD-16X2 [package=lcd-16x2_noholes]
  R1 = Trimmer Potentiometer [maximum_resistance=10kΩ knob_status=50% power=0.5W package=THT]  # not connected
  R2 = Resistor [tolerance=±5% power=0.25 resistance=220 package=THT]

nets:
  GND: Part1.GND, U1.VSS, U1.K
  5V: Part1.5V, U1.VDD, U1.R_W, R2.Pin_0
  N1: Part1.D22, U1.RS
  N2: Part1.D23, Keypad4x1.Pin1
  N3: Part1.D24, U1.E
  N4: Part1.D25, Keypad4x1.Pin2
  N5: Part1.D26, U1.DB4
  N6: Part1.D27, Keypad4x1.Pin3
  N7: Part1.D28, U1.DB5
  N8: Part1.D29, Keypad4x1.Pin4
  N9: Part1.D30, U1.DB6
  N10: Part1.D31, Keypad4x1.Pin5
  N11: Part1.D32, U1.DB7
  N12: Part1.D33, Keypad4x1.Pin6
  N13: Part1.D35, Keypad4x1.Pin7
  N14: Part1.D37, Keypad4x1.Pin8
  N15: U1.A, R2.Pin_1

custom parts:
  Arduino Mega 2560 (Rev3): The Arduino Mega 2560 is a microcontroller board based on the ATmega2560 (datasheet). It has 54 digital input/output pins (of which 14 can be used as PWM outputs), 16 analog inputs, 4 UARTs (hardware serial ports), a 16 MHz crystal oscillator, a USB connection, a power jack, an ICSP header, and a reset button. It contains everything needed to support the microcontroller; simply connect it to a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
  Keypad Membran 4x4: Membrane Keypad 4x4 Matrix
