# Fritzing sketch 40_RFID-DoorLocks (saved by Fritzing 0.9.10b)
breadboards: 1

parts:
  Part1 = Arduino Mega 2560 (Rev3)
  U1 = LCD-16X2 [package=lcd-16x2_noholes]
  R1 = Trimmer Potentiometer [maximum_resistance=10kΩ knob_status=50% power=0.5W package=THT]
  R2 = Resistor [tolerance=±5% power=0.25 resistance=220 package=THT]
  Part2 = RFID-RC522-v2

nets:
  3V3: Part1.3V3, Part2.3.3V
  5V: Part1.5V, U1.VDD, R1.leg2, R2.Pin_0
  N1: Part1.D22, U1.RS
  N2: Part1.D23, U1.DB4
  N3: Part1.D24, U1.E
  N4: Part1.D25, U1.DB5
  N5: Part1.D26, Part2.RST
  N6: Part1.D27, U1.DB6
  N7: Part1.D29, U1.DB7
  N8: Part1.D50, Part2.MISO
  N9: Part1.D51, Part2.MOSI
  N10: Part1.D52, Part2.SCK
  N11: Part1.D53, Part2.SDA
  GND: Part1.GND, U1.VSS, U1.R_W, U1.K, R1.leg1, Part2.GND
  N12: U1.VO, R1.wiper
  N13: U1.A, R2.Pin_1

notes:
  RFID requires 3.3V

custom parts:
  Arduino Mega 2560 (Rev3): The Arduino Mega 2560 is a microcontroller board based on the ATmega2560 (datasheet). It has 54 digital input/output pins (of which 14 can be used as PWM outputs), 16 analog inputs, 4 UARTs (hardware serial ports), a 16 MHz crystal oscillator, a USB connection, a power jack, an ICSP header, and a reset button. It contains everything needed to support the microcontroller; simply connect it to a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
  RFID-RC522-v2: A simple China made RFID-RC522 Reader; do check the pin labels, as this is a MFRC522 based clone.
