# Fritzing sketch DryPlantAlertSystem (saved by Fritzing 0.9.10b)
breadboards: 1

parts:
  Water_Level_Sensor1 = Water Level Sensor
  Part1 = Arduino Mega 2560 (Rev3)
  LED1 = LED - 5mm [color="Red (633nm)" current=0.030 package="5 mm [THT]"]
  R1 = Resistor [tolerance=±5% power=0.25 resistance=220 package=THT]

nets:
  N1: Water_Level_Sensor1.SIG, Part1.A8
  VCC: Water_Level_Sensor1.VCC, Part1.5V
  GND: Water_Level_Sensor1.GND, Part1.GND, LED1.cathode
  N2: Part1.D22, R1.Pin_1
  N3: LED1.anode, R1.Pin_0

custom parts:
  Water Level Sensor: A water level sensor. This sensor operates at 3V to 5V. The Sig (signal) pin outputs an analogue signal that is in proportion to the amount of water in contact with the sensor.
  Arduino Mega 2560 (Rev3): The Arduino Mega 2560 is a microcontroller board based on the ATmega2560 (datasheet). It has 54 digital input/output pins (of which 14 can be used as PWM outputs), 16 analog inputs, 4 UARTs (hardware serial ports), a 16 MHz crystal oscillator, a USB connection, a power jack, an ICSP header, and a reset button. It contains everything needed to support the microcontroller; simply connect it to a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
