# Fritzing sketch accuratealarmclock (saved by Fritzing 0.9.10b)
breadboards: 1

parts:
  7_Segment_4_Digit_Display1 = 7-SEGMENT-4DIGIT common anode [part_number="5461BS - 5462BS" package=7-segment-4digit-anode]
  R1 = Resistor [tolerance=±5% resistance=220 package="0402 [SMD]"]
  R2 = Resistor [tolerance=±5% resistance=220 package="0402 [SMD]"]
  R3 = Resistor [tolerance=±5% resistance=220 package="0402 [SMD]"]
  R4 = Resistor [tolerance=±5% resistance=220 package="0402 [SMD]"]
  Part2 = Arduino Mega 2560 (Rev3)
  ZS-042_RTC1 = ZS-042 RTC Module
  SG1 = Buzzer 12mm [part_number=COM-07950 package=buzzer-12mm-ns]

nets:
  N1: 7_Segment_4_Digit_Display1.pin_1, Part2.D10_PWM
  N2: 7_Segment_4_Digit_Display1.pin_2, Part2.D9_PWM
  N3: 7_Segment_4_Digit_Display1.pin_3, Part2.D13_PWM
  N4: 7_Segment_4_Digit_Display1.pin_4, Part2.D8_PWM
  N5: 7_Segment_4_Digit_Display1.pin_5, Part2.D12_PWM
  N6: 7_Segment_4_Digit_Display1.pin_6, R1.Pin_0
  N7: 7_Segment_4_Digit_Display1.pin_7, Part2.D7_PWM
  N8: 7_Segment_4_Digit_Display1.pin_8, R2.Pin_0
  N9: 7_Segment_4_Digit_Display1.pin_9, R3.Pin_0
  N10: 7_Segment_4_Digit_Display1.pin_10, Part2.D11_PWM
  N11: 7_Segment_4_Digit_Display1.pin_11, Part2.D6_PWM
  N12: 7_Segment_4_Digit_Display1.pin_12, R4.Pin_0
  N13: R1.Pin_1, Part2.D5_PWM
  N14: R2.Pin_1, Part2.D4_PWM
  N15: R3.Pin_1, Part2.D3_PWM
  N16: R4.Pin_1, Part2.D2_PWM
  N17: Part2.D21/SCL, ZS-042_RTC1.SCL
  N18: Part2.D20/SDA, ZS-042_RTC1.SDA
  GND: Part2.GND, ZS-042_RTC1.GND, SG1.2
  5V: Part2.5V, ZS-042_RTC1.VCC
  N19: Part2.D45, SG1.1

notes:
  Need at least 4 220ohm Resistors

custom parts:
  7-SEGMENT-4DIGIT common anode: A 7 Segment 4 Digit common anode display, with decimal points
  Arduino Mega 2560 (Rev3): The Arduino Mega 2560 is a microcontroller board based on the ATmega2560 (datasheet). It has 54 digital input/output pins (of which 14 can be used as PWM outputs), 16 analog inputs, 4 UARTs (hardware serial ports), a 16 MHz crystal oscillator, a USB connection, a power jack, an ICSP header, and a reset button. It contains everything needed to support the microcontroller; simply connect it to a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
  Buzzer 12mm: Buzzer 12mm Spark Fun Electronics SKU : Comp-Buzzer Through hole This is a small 12mm round speaker that operates around the audible 2kHz range. You can use these speakers to create simple music or user interfaces. This is not a true piezoelectric speaker but behaves similarly. Instead of a piezoelectric crystal that vibrates with an electric current, this tiny speaker uses an electromagnet to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
