# Fritzing sketch IR-SmartLights (saved by Fritzing 0.9.10b)
breadboards: 1

parts:
  Part1 = Arduino Mega 2560 (Rev3)
  Mod1 = KY-022 Infrared Receiver Module [package="Breakout board"]
  LED1 = RGB LED (com. cathode, rgb) [package="5 mm [THT]"]
  R1 = Resistor [tolerance=±5% resistance=220 package="0603 [SMD]"]
  R2 = Resistor [tolerance=±5% resistance=220 package="0603 [SMD]"]
  R3 = Resistor [tolerance=±5% resistance=220 package="0603 [SMD]"]

nets:
  5V: Part1.5V, Mod1.Vin
  N1: Part1.D22, R1.Pin_1
  N2: Part1.D24, R2.Pin_1
  N3: Part1.D26, R3.Pin_1
  N4: Part1.D28, Mod1.S
  N5: Part1.GND, Mod1.-, LED1.common_cathode
  N6: LED1.red_anode, R1.Pin_0
  N7: LED1.green_anode, R2.Pin_0
  N8: LED1.blue_anode, R3.Pin_0

custom parts:
  Arduino Mega 2560 (Rev3): The Arduino Mega 2560 is a microcontroller board based on the ATmega2560 (datasheet). It has 54 digital input/output pins (of which 14 can be used as PWM outputs), 16 analog inputs, 4 UARTs (hardware serial ports), a 16 MHz crystal oscillator, a USB connection, a power jack, an ICSP header, and a reset button. It contains everything needed to support the microcontroller; simply connect it to a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
  KY-022 Infrared Receiver Module: KY-022 IR receiver module, reacts to 38kHz infrared light.
