# Fritzing sketch 10_WIFI-LightControlAP (saved by Fritzing 0.9.10b)
breadboards: 1

parts:
  Mod1 = ESP32-TTGO-T-DISPLAY
  R1 = Resistor [tolerance=±5% power=0.25 resistance=220 package=THT]
  LED1 = smd LED [color="Red (633nm)" package="0603 [SMD]"]

nets:
  N1: Mod1.G-1, Mod1.G-2, Mod1.G-10, Mod1.G-11, Mod1.G-14, R1.Pin_0
  N2: Mod1.2, LED1.anode
  N3: R1.Pin_1, LED1.cathode

custom parts:
  ESP32-TTGO-T-DISPLAY: LILYGO TTGO T-Display GD32VF103CBT6 Main Chip ST7789 1.14 Inch IPS 240x135 Resolution Minimalist Development Board.
