# Fritzing sketch 20-180_DegreeSonar (saved by Fritzing 0.9.10b)
breadboards: 1

parts:
  Part1 = Arduino Mega 2560 (Rev3)
  Part2 = 2.4 Touchscreen TFT Breakout w:MicroSD
  SERVO1 = Tower Pro SG90 servo [part_number=101246]
  Part3 = SRF05 Ultrasonic Rangefinder
  VCC1 = Battery block 9V  # not connected

nets:
  N1: Part1.A0, Part2.X+
  N2: Part1.A1, Part1.D5_PWM, Part2.Y-
  N3: Part1.A2, Part1.D6_PWM, Part2.X-
  N4: Part1.A3, Part2.IM0
  N5: Part1.A4, Part2.IM1
  N6: Part1.A5, Part2.IM2
  N7: Part1.A6, Part2.IM3
  N8: Part1.A7, Part2.SD_CS
  N9: Part1.D15/RX3, Part2.D7
  N10: Part1.D14/TX3, Part2.D6
  N11: Part1.IOREF#254, Part2.+3V
  N12: Part1.IOREF#255, Part2.C/D, Part2.CLK
  N13: Part1.RESET, Part2.MISO
  N14: Part1.3V3, Part2.MOSI
  5V: Part1.5V, Part2.CS, SERVO1.+5V, Part3.VCC
  GND: Part1.GND, Part2.WR_DC, Part2.RST, SERVO1.GND, Part3.GND
  N15: Part1.VIN, Part2.LITE
  N16: Part1.D0_RX0, Part2.D4
  N17: Part1.D1_TX0, Part2.D3
  N18: Part1.D2_PWM, Part2.D2
  N19: Part1.D3_PWM, Part2.D1
  N20: Part1.D4_PWM, Part2.D0
  N21: Part1.D7_PWM, Part2.Y+
  N22: Part1.D22, Part3.Trig
  N23: Part1.D23, Part3.Echo
  N24: Part1.D24, SERVO1.Signal

custom parts:
  Arduino Mega 2560 (Rev3): The Arduino Mega 2560 is a microcontroller board based on the ATmega2560 (datasheet). It has 54 digital input/output pins (of which 14 can be used as PWM outputs), 16 analog inputs, 4 UARTs (hardware serial ports), a 16 MHz crystal oscillator, a USB connection, a power jack, an ICSP header, and a reset button. It contains everything needed to support the microcontroller; simply connect it to a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
  2.4 Touchscreen TFT Breakout w:MicroSD: Add some jazz & pizzazz to your project with a color touchscreen LCD. This TFT display is 2.4" diagonal with a bright (4 white-LED) backlight and it's colorful! 240x320 pixels with individual RGB pixel control, this has way more resolution than a black and white 128x64 display. As a bonus, this display has a resistive touchscreen attached to it already, so you can detect finger presses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
  Tower Pro SG90 servo: Original file by John De Cristofaro http://www.adafruit.com/products/1449 Adafruit Feedback Servo (Small) Edited by: e-radionica.com 28/9/2015
