# Fritzing sketch 30-RGB_TurretGun (saved by Fritzing 0.9.10b)
breadboards: 1

parts:
  Part1 = Arduino Mega 2560 (Rev3)
  VCC1 = Battery block 9V  # not connected
  YwRobot_Power_Supply1 = YwRobot Breadboard Power Supply [part_number=545043]
  SM1 = 28BYJ-48 Stepper Motor [part_number=28BYJ-48]  # not connected
  Mod1 = KY-023 Dual Axis Joystick Module [package="Breakout board"]
  LED5 = RGB LED - (4 legs) [package="5 mm [THT]"]
  Driver1 = 28BYJ-48 Driver Module [part_number=ULN2003 package=THT]
  R1 = Resistor [tolerance=±5% resistance=220 package="0402 [SMD]"]
  R2 = Resistor [tolerance=±5% resistance=220 package="0402 [SMD]"]
  R3 = Resistor [tolerance=±5% resistance=220 package="0402 [SMD]"]

nets:
  N1: Part1.A8, Mod1.VRx
  GND: Part1.GND, YwRobot_Power_Supply1.GND#13, YwRobot_Power_Supply1.GND#14, Mod1.GND, LED5.common_anode, Driver1.GND
  5V: Part1.5V, Mod1.+5V
  N2: Part1.D22, Driver1.IN1
  N3: Part1.D24, Driver1.IN2
  N4: Part1.D26, Driver1.IN3
  N5: Part1.D28, Driver1.IN4
  N6: Part1.D30, Mod1.SW
  N7: Part1.D44, R1.Pin_1
  N8: Part1.D45, R3.Pin_1
  N9: Part1.D46, R2.Pin_1
  N10: YwRobot_Power_Supply1.VCC#5, YwRobot_Power_Supply1.VCC#6
  N11: YwRobot_Power_Supply1.VCC#9, YwRobot_Power_Supply1.VCC#10, Driver1.Vmotor
  N12: YwRobot_Power_Supply1.GND#11, YwRobot_Power_Supply1.GND#12
  N13: LED5.red_cathode, R1.Pin_0
  N14: LED5.green_cathode, R3.Pin_0
  N15: LED5.blue_cathode, R2.Pin_0

notes:
  Stepper cannot be safely powered directly from HERO XL so use breadboard power supply and 9V battery.

custom parts:
  Arduino Mega 2560 (Rev3): The Arduino Mega 2560 is a microcontroller board based on the ATmega2560 (datasheet). It has 54 digital input/output pins (of which 14 can be used as PWM outputs), 16 analog inputs, 4 UARTs (hardware serial ports), a 16 MHz crystal oscillator, a USB connection, a power jack, an ICSP header, and a reset button. It contains everything needed to support the microcontroller; simply connect it to a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
  YwRobot Breadboard Power Supply: The YwRobot Breadboard Power Supply (MB-V2) has two power rails; they can be 5V or 3V3. Power to the module can be provided through the female USB socket or through the A10 (female) 2.1mm power jack.
  28BYJ-48 Stepper Motor: Unipolar Stepper Motor 28BYJ-48 Top coil - pink & orange Bottom coil - blue & yellow Common rail - red Connector pins: blue - pink - yellow - orange - red
  KY-023 Dual Axis Joystick Module: KY-023 Dual-Axis Joystick Module.
  28BYJ-48 Driver Module: ULN2003 Driver Module for the 28BYJ-48 Unipolar Stepper Motor LED A - Blue wire - Bottom coil left LED B - Pink wire - Top coil left LED C - Yellow wire - Bottom coil right LED D - Orange wire - Top coil right Common rail - red Connector pins: blue - pink - yellow - orange - red Control pins - IN1 to IN4 Power pins - GND & Vmotor (5-12V) On/Off jumper (if removed, power to motor is cut).
