# Fritzing sketch 40-RGB_TurretGun_T-Display (saved by Fritzing 0.9.10b)
breadboards: 1

parts:
  VCC1 = Battery block 9V  # not connected
  YwRobot_Power_Supply1 = YwRobot Breadboard Power Supply [part_number=545043]
  SM1 = 28BYJ-48 Stepper Motor [part_number=28BYJ-48]  # not connected
  Mod1 = KY-023 Dual Axis Joystick Module [package="Breakout board"]
  LED5 = RGB LED - (4 legs) [package="5 mm [THT]"]
  Driver1 = 28BYJ-48 Driver Module [part_number=ULN2003 package=THT]
  R1 = Resistor [tolerance=±5% resistance=220 package="0402 [SMD]"]
  R2 = Resistor [tolerance=±5% resistance=220 package="0402 [SMD]"]
  R3 = Resistor [tolerance=±5% resistance=220 package="0402 [SMD]"]
  Mod2 = ESP32-TTGO-T-DISPLAY

nets:
  N1: YwRobot_Power_Supply1.VCC#5, YwRobot_Power_Supply1.VCC#6
  N2: YwRobot_Power_Supply1.VCC#9, YwRobot_Power_Supply1.VCC#10, Driver1.Vmotor
  N3: YwRobot_Power_Supply1.GND#11, YwRobot_Power_Supply1.GND#12
  GND: YwRobot_Power_Supply1.GND#13, YwRobot_Power_Supply1.GND#14, Mod1.GND, LED5.common_anode, Driver1.GND, Mod2.G-1, Mod2.G-2, Mod2.G-10, Mod2.G-11, Mod2.G-14
  N4: Mod1.+5V, Mod2.3V
  N5: Mod1.VRx, Mod2.36
  N6: Mod1.SW, Mod2.27
  N7: LED5.red_cathode, R1.Pin_0
  N8: LED5.green_cathode, R3.Pin_0
  N9: LED5.blue_cathode, R2.Pin_0
  N10: Driver1.IN1, Mod2.2
  N11: Driver1.IN2, Mod2.17
  N12: Driver1.IN3, Mod2.22
  N13: Driver1.IN4, Mod2.21
  N14: R1.Pin_1, Mod2.32
  N15: R2.Pin_1, Mod2.25
  N16: R3.Pin_1, Mod2.33

notes:
  Stepper cannot be safely powered directly from HERO XL so use breadboard power supply and 9V battery.

custom parts:
  YwRobot Breadboard Power Supply: The YwRobot Breadboard Power Supply (MB-V2) has two power rails; they can be 5V or 3V3. Power to the module can be provided through the female USB socket or through the A10 (female) 2.1mm power jack.
  28BYJ-48 Stepper Motor: Unipolar Stepper Motor 28BYJ-48 Top coil - pink & orange Bottom coil - blue & yellow Common rail - red Connector pins: blue - pink - yellow - orange - red
  KY-023 Dual Axis Joystick Module: KY-023 Dual-Axis Joystick Module.
  28BYJ-48 Driver Module: ULN2003 Driver Module for the 28BYJ-48 Unipolar Stepper Motor LED A - Blue wire - Bottom coil left LED B - Pink wire - Top coil left LED C - Yellow wire - Bottom coil right LED D - Orange wire - Top coil right Common rail - red Connector pins: blue - pink - yellow - orange - red Control pins - IN1 to IN4 Power pins - GND & Vmotor (5-12V) On/Off jumper (if removed, power to motor is cut).
  ESP32-TTGO-T-DISPLAY: LILYGO TTGO T-Display GD32VF103CBT6 Main Chip ST7789 1.14 Inch IPS 240x135 Resolution Minimalist Development Board.
